// Logisim project ProcessorCore.circ as structural Verilog: 22 circuits, main circuit main
module main (
  input  reset
);

  wire ALU_z, ALUinB, and_1_out, and_2_out, BEQZ, BGT, clk, DMwe, gt, \input , JAL, JP, JR, keyboard_1_avail,
       not_1_out, not_2_out, or_1_out, \output , Rdst, Rwd, Rwe;
  wire [2:0] ALUinOP;
  wire [3:0] multiplexer_1_out, multiplexer_2_out, opcode;
  wire [6:0] keyboard_1_data, Register_File_rs1val;
  wire [7:7] not_3_out;
  wire [11:0] address, PC_currentregister;
  wire [15:0] ALU_output, dd, intoReg, multiplexer_4_out, multiplexer_5_out, multiplexer_6_out,
       multiplexer_7_out, multiplexer_8_out, n16_bit_adder_2_sum, PC_1, ram_1_data, Register_File_rs2val,
       SX_output;
  wire [15:7] Register_File_rs1val_2;
  wire [15:12] jump_address;

  Clock clock_1 (.out(clk));
  Register PC (
    .reset(reset), .clock(clk), .WE(1'b1), .Data(multiplexer_7_out),
    .currentRegister({jump_address, PC_currentregister}));
  Control control_1 (
    .opcode(opcode), .\output (\output ), .\input (\input ), .JAL(JAL), .DMwe(DMwe), .JP(JP), .BEQZ(BEQZ),
    .Rwe(Rwe), .Rwd(Rwd), .Rdst(Rdst), .ALUinOP(ALUinOP), .ALUinB(ALUinB), .JR(JR), .BGT(BGT));
  ROM #(.addrWidth(16), .dataWidth(16)) rom_1 (
    .addr({jump_address, PC_currentregister}), .data({opcode, address}));  // open: sel
  Multiplexer #(.width(4), .enable("false")) multiplexer_1 (
    .in0(multiplexer_2_out), .in1(4'b0111), .out(multiplexer_1_out), .sel(JAL));
  Multiplexer #(.width(4), .enable("false")) multiplexer_2 (
    .in0({1'b0, address[8:6]}), .in1({1'b0, address[5:3]}), .out(multiplexer_2_out), .sel(Rdst));
  not not_1 (not_1_out, clk);
  regfile Register_File (
    .s1({1'b0, address[11:9]}), .s2({1'b0, address[8:6]}), .d(multiplexer_1_out), .WriteData(intoReg),
    .clock(not_1_out), .Write(Rwe), .in_6(reset), .RS1VAL({Register_File_rs1val_2, Register_File_rs1val}),
    .RS2VAL(Register_File_rs2val));
  Multiplexer #(.width(16), .enable("false")) multiplexer_3 (.in0(multiplexer_6_out), .in1(PC_1), .out(dd), .sel(JAL));
  SX SX (.\input (address[5:0]), .\output (SX_output));
  _16_bit_adder u_16_bit_adder_1 (
    .Cin(1'b0), .in_2({jump_address, PC_currentregister}), .in_3(16'h1), .sub(1'b0), .Sum(PC_1));  // open: Cout
  Multiplexer #(.width(16), .enable("false")) multiplexer_4 (
    .in0(Register_File_rs2val), .in1(SX_output), .out(multiplexer_4_out), .sel(ALUinB));
  _16_bit_adder u_16_bit_adder_2 (
    .Cin(1'b0), .in_2(PC_1), .in_3(SX_output), .sub(1'b0), .Sum(n16_bit_adder_2_sum));  // open: Cout
  and and_1 (and_1_out, ALU_z, BEQZ);
  ALU ALU (
    .switch(ALUinOP), .a({Register_File_rs1val_2, Register_File_rs1val}), .b(multiplexer_4_out),
    .shift(address[2:0]), .greater_than(gt), .\output (ALU_output), .Z(ALU_z));  // open: Cout
  or or_1 (or_1_out, and_1_out, and_2_out);
  and and_2 (and_2_out, gt, BGT);
  not not_2 (not_2_out, clk);
  TTY #(.rows(13), .cols(80), .trigger("falling")) tty_1 (
    .data(Register_File_rs1val), .clk(clk), .we(\output ), .clr(reset));
  Multiplexer #(.width(16), .enable("false")) multiplexer_5 (
    .in0(PC_1), .in1(n16_bit_adder_2_sum), .out(multiplexer_5_out), .sel(or_1_out));
  Multiplexer #(.width(16), .enable("false")) multiplexer_6 (
    .in0(ALU_output), .in1(ram_1_data), .out(multiplexer_6_out), .sel(Rwd));
  RAM #(.addrWidth(16), .dataWidth(16), .bus("separate")) ram_1 (
    .addr(ALU_output), .din(Register_File_rs2val), .data(ram_1_data), .str(DMwe), .clk(not_2_out));  // open: sel, ld, clr
  Multiplexer #(.width(16), .enable("false")) multiplexer_7 (
    .in0(multiplexer_5_out), .in1(multiplexer_8_out), .out(multiplexer_7_out), .sel(JP));
  Multiplexer #(.width(16), .enable("false")) multiplexer_8 (
    .in0({jump_address, address}), .in1({Register_File_rs1val_2, Register_File_rs1val}),
    .out(multiplexer_8_out), .sel(JR));
  Keyboard keyboard_1 (.clk(clk), .re(\input ), .clr(reset), .avail(keyboard_1_avail), .data(keyboard_1_data));
  not not_3 (not_3_out[7], keyboard_1_avail);
  Multiplexer #(.width(16), .enable("false")) multiplexer_9 (
    .in0(dd), .in1({{8{1'b0}}, not_3_out[7], keyboard_1_data}), .out(intoReg), .sel(\input ));

  // Other names for the same wires on the sheet: jump_address[11:0] = address; immed[5:0] = address[5:0]

  // Notes on the sheet:
  //   contents of rom_1 (hex, n*v repeats v):
  //   2040 620d 2240 620d 2240 6209 2240 d021 f028 ea00 2040 620d 2240 620d 2243 6209 2241 9280 a344 9304
  //   3860 e800 4558 213f 1528 568 6432 5432 24be 5811 7401 3410 803f 92c0 8603 e600 2241 b021 ce00
endmodule

module _1_bit_adder (
  input  Cin,
  input  A,
  input  B,
  input  sub,
  output Sum,
  output Cout
);

  wire and_1_out, and_2_out, xor_1_out, xor_2_out;

  xor xor_1 (xor_1_out, B, sub);
  and and_1 (and_1_out, A, xor_1_out);
  xor xor_2 (xor_2_out, A, xor_1_out);
  and and_2 (and_2_out, Cin, xor_2_out);
  xor xor_3 (Sum, Cin, xor_2_out);
  or or_1 (Cout, and_2_out, and_1_out);
endmodule

module _2_bit_adder (
  input  Cin,
  input  [1:0] a,
  input  [1:0] b,
  input  sub,
  output [1:0] Sum,
  output Cout
);

  wire n1_bit_adder_1_cout;

  _1_bit_adder u_1_bit_adder_1 (.Cin(Cin), .A(a[0]), .B(b[0]), .sub(sub), .Sum(Sum[0]), .Cout(n1_bit_adder_1_cout));
  _1_bit_adder u_1_bit_adder_2 (.Cin(n1_bit_adder_1_cout), .A(a[1]), .B(b[1]), .sub(sub), .Sum(Sum[1]), .Cout(Cout));
endmodule

module _4_bit_adder (
  input  Cin,
  input  [3:0] a,
  input  [3:0] b,
  input  sub,
  output [3:0] Sum,
  output Cout
);

  wire n2_bit_adder_1_cout;

  _2_bit_adder u_2_bit_adder_1 (
    .Cin(Cin), .a(a[1:0]), .b(b[1:0]), .sub(sub), .Sum(Sum[1:0]), .Cout(n2_bit_adder_1_cout));
  _2_bit_adder u_2_bit_adder_2 (
    .Cin(n2_bit_adder_1_cout), .a(a[3:2]), .b(b[3:2]), .sub(sub), .Sum(Sum[3:2]), .Cout(Cout));
endmodule

module _8_bit_adder (
  input  Cin,
  input  [7:0] a,
  input  [7:0] b,
  input  sub,
  output [7:0] Sum,
  output Cout
);

  wire n4_bit_adder_1_cout;

  _4_bit_adder u_4_bit_adder_1 (
    .Cin(Cin), .a(a[3:0]), .b(b[3:0]), .sub(sub), .Sum(Sum[3:0]), .Cout(n4_bit_adder_1_cout));
  _4_bit_adder u_4_bit_adder_2 (
    .Cin(n4_bit_adder_1_cout), .a(a[7:4]), .b(b[7:4]), .sub(sub), .Sum(Sum[7:4]), .Cout(Cout));
endmodule

module _16_bit_adder (
  input  Cin,
  input  [15:0] in_2,
  input  [15:0] in_3,
  input  sub,
  output [15:0] Sum,
  output Cout
);

  wire n8_bit_adder_1_cout;

  _8_bit_adder u_8_bit_adder_1 (
    .Cin(Cin), .a(in_2[7:0]), .b(in_3[7:0]), .sub(sub), .Sum(Sum[7:0]), .Cout(n8_bit_adder_1_cout));
  _8_bit_adder u_8_bit_adder_2 (
    .Cin(n8_bit_adder_1_cout), .a(in_2[15:8]), .b(in_3[15:8]), .sub(sub), .Sum(Sum[15:8]), .Cout(Cout));
endmodule

module _2x1MUX (
  input  a,
  input  b,
  input  s,
  output \output 
);

  Multiplexer #(.enable("false")) multiplexer_1 (.in0(a), .in1(b), .out(\output ), .sel(s));
endmodule

module _3_bit_arithmetic_right_shift (
  input  [15:0] \input ,
  input  [2:0] shift,
  output [15:0] \output 
);

  wire [15:0] multiplexer_1_out, multiplexer_2_out;

  Multiplexer #(.width(16), .enable("false")) multiplexer_1 (
    .in0(\input ), .in1({{5{\input [15]}}, \input [14:4]}), .out(multiplexer_1_out), .sel(shift[2]));
  Multiplexer #(.width(16), .enable("false")) multiplexer_2 (
    .in0(multiplexer_1_out), .in1({{3{multiplexer_1_out[15]}}, multiplexer_1_out[14:2]}),
    .out(multiplexer_2_out), .sel(shift[1]));
  Multiplexer #(.width(16), .enable("false")) multiplexer_3 (
    .in0(multiplexer_2_out), .in1({{2{multiplexer_2_out[15]}}, multiplexer_2_out[14:1]}), .out(\output ),
    .sel(shift[0]));
endmodule

module _3_bit_left_logical (
  input  [15:0] \input ,
  input  [2:0] shift,
  output [15:0] \output 
);

  wire [15:0] multiplexer_1_out, multiplexer_2_out;

  Multiplexer #(.width(16), .enable("false")) multiplexer_1 (
    .in0(\input ), .in1({\input [11:0], 4'b0000}), .out(multiplexer_1_out), .sel(shift[2]));
  Multiplexer #(.width(16), .enable("false")) multiplexer_2 (
    .in0(multiplexer_1_out), .in1({multiplexer_1_out[13:0], 2'b00}), .out(multiplexer_2_out), .sel(shift[1]));
  Multiplexer #(.width(16), .enable("false")) multiplexer_3 (
    .in0(multiplexer_2_out), .in1({multiplexer_2_out[14:0], 1'b0}), .out(\output ), .sel(shift[0]));
endmodule

module ALU (
  input  [2:0] switch,
  input  [15:0] a,
  input  [15:0] b,
  input  [2:0] shift,
  output Cout,
  output [15:0] \output ,
  output Z,
  output greater_than
);

  wire n16_bit_adder_1_cout, n16_bit_adder_2_cout, n16_bit_adder_3_cout, not_1_out, not_2_out, or_2_out,
       or_3_out;
  wire [15:0] n1_to_16_bit_extender_1_out_2, n3_bit_arithmetic_right_shift_1_output,
       n3_bit_left_logical_1_output, n16_bit_adder_1_sum, n16_bit_adder_2_sum, n16_bit_adder_3_sum,
       nand_1_out, xor_1_out;

  not not_1 (not_1_out, 1'b0);
  assign nand_1_out = ~(a & b);  // NAND_Gate nand_1, 16 bits wide
  assign xor_1_out = a ^ b;  // XOR_Gate xor_1, 16 bits wide
  _3_bit_arithmetic_right_shift u_3_bit_arithmetic_right_shift_1 (
    .\input (a), .shift(shift), .\output (n3_bit_arithmetic_right_shift_1_output));
  _3_bit_left_logical u_3_bit_left_logical_1 (.\input (a), .shift(shift), .\output (n3_bit_left_logical_1_output));
  _16_bit_adder u_16_bit_adder_1 (
    .Cin(1'b0), .in_2(a), .in_3(b), .sub(1'b0), .Sum(n16_bit_adder_1_sum), .Cout(n16_bit_adder_1_cout));
  _16_bit_adder u_16_bit_adder_2 (
    .Cin(1'b0), .in_2(a), .in_3(b), .sub(1'b0), .Sum(n16_bit_adder_2_sum), .Cout(n16_bit_adder_2_cout));
  _16_bit_adder u_16_bit_adder_3 (
    .Cin(not_1_out), .in_2(a), .in_3(b), .sub(not_1_out), .Sum(n16_bit_adder_3_sum),
    .Cout(n16_bit_adder_3_cout));
  or or_1 (Cout, n16_bit_adder_3_cout, n16_bit_adder_1_cout, n16_bit_adder_2_cout);
  _1_to_16_bit_extender u_1_to_16_bit_extender_1 (._1_bit_input(1'b0), .out_2(n1_to_16_bit_extender_1_out_2));
  Multiplexer #(.select(3), .width(16), .enable("false")) multiplexer_1 (
    .in0(nand_1_out), .in1(xor_1_out), .in2(n16_bit_adder_1_sum), .in3(n16_bit_adder_2_sum),
    .in4(n16_bit_adder_3_sum), .in5(n3_bit_arithmetic_right_shift_1_output),
    .in6(n3_bit_left_logical_1_output), .in7(n1_to_16_bit_extender_1_out_2), .out(\output ), .sel(switch));
  not not_2 (not_2_out, n16_bit_adder_3_sum[15]);
  and and_1 (greater_than, not_2_out, or_3_out);
  or or_2 (or_2_out, a[15], a[14], a[13], a[12], a[11], a[10], a[9], a[8], a[6], a[5], a[4], a[3], a[2], a[1], a[7], a[0]);
  not not_3 (Z, or_2_out);
  or or_3 (or_3_out, n16_bit_adder_3_sum[14], n16_bit_adder_3_sum[13], n16_bit_adder_3_sum[12], n16_bit_adder_3_sum[11], n16_bit_adder_3_sum[10], n16_bit_adder_3_sum[9], n16_bit_adder_3_sum[8], n16_bit_adder_3_sum[7], n16_bit_adder_3_sum[6], n16_bit_adder_3_sum[5], n16_bit_adder_3_sum[4], n16_bit_adder_3_sum[3], n16_bit_adder_3_sum[2], n16_bit_adder_3_sum[1], n16_bit_adder_3_sum[0]);

  // Other names for the same wires on the sheet: rs[15:0] = a
endmodule

module _4x1MUX (
  input  [15:0] a,
  input  [15:0] b,
  input  [15:0] c,
  input  [15:0] d,
  input  [1:0] s0,
  output [15:0] out
);

  wire [15:0] multiplexer_1_out, multiplexer_2_out;

  Multiplexer #(.width(16), .enable("false")) multiplexer_1 (.in0(a), .in1(b), .out(multiplexer_1_out), .sel(s0[0]));
  Multiplexer #(.width(16), .enable("false")) multiplexer_2 (.in0(c), .in1(d), .out(multiplexer_2_out), .sel(s0[0]));
  Multiplexer #(.width(16), .enable("false")) multiplexer_3 (
    .in0(multiplexer_1_out), .in1(multiplexer_2_out), .out(out), .sel(s0[1]));
endmodule

module _8x1MUX (
  input  [15:0] a,
  input  [15:0] b,
  input  [15:0] c,
  input  [15:0] d,
  input  [15:0] e,
  input  [15:0] f,
  input  [15:0] g,
  input  [15:0] h,
  input  [2:0] s0,
  output [15:0] out
);

  wire [15:0] n4x1mux_1_out, n4x1mux_2_out;

  _4x1MUX u_4x1mux_1 (.a(a), .b(b), .c(c), .d(d), .s0(s0[1:0]), .out(n4x1mux_1_out));
  _4x1MUX u_4x1mux_2 (.a(e), .b(f), .c(g), .d(h), .s0(s0[1:0]), .out(n4x1mux_2_out));
  Multiplexer #(.width(16), .enable("false")) multiplexer_1 (
    .in0(n4x1mux_1_out), .in1(n4x1mux_2_out), .out(out), .sel(s0[2]));
endmodule

module _1_to_16_bit_extender (
  input  _1_bit_input,
  output [15:0] out_2
);


  assign out_2 = {{15{1'b0}}, _1_bit_input};
endmodule

module regfile (
  input  clock,
  input  Write,
  input  [3:0] s1,
  input  [3:0] s2,
  input  [3:0] d,
  input  in_6,
  input  [15:0] WriteData,
  output [15:0] RS1VAL,
  output [15:0] RS2VAL
);

  wire and_2_out, and_3_out, and_4_out, and_5_out, and_6_out, and_7_out, and_8_out, and_9_out, and_10_out,
       and_11_out, and_12_out, and_13_out, and_14_out, and_15_out, and_16_out;
  wire [15:0] _0_currentregister, _2_currentregister, _4_currentregister, _6_currentregister,
       _8_currentregister, _10_currentregister, _12_currentregister, _14_currentregister,
       n4_to_16_decoder_1_out, register_1_currentregister, register_2_currentregister,
       register_3_currentregister, register_4_currentregister, register_5_currentregister,
       register_6_currentregister, register_7_currentregister, register_8_currentregister;

  _4_to_16_Decoder u_4_to_16_decoder_1 (.\input (d), .out(n4_to_16_decoder_1_out));
  // AND_Gate and_1 has open pins: in2=Write, in4=n4_to_16_decoder_1_out[0], out=open
  and and_2 (and_2_out, Write, n4_to_16_decoder_1_out[1]);
  and and_3 (and_3_out, Write, n4_to_16_decoder_1_out[2]);
  and and_4 (and_4_out, n4_to_16_decoder_1_out[3], Write);
  and and_5 (and_5_out, n4_to_16_decoder_1_out[4], Write);
  and and_6 (and_6_out, Write, n4_to_16_decoder_1_out[5]);
  and and_7 (and_7_out, Write, n4_to_16_decoder_1_out[6]);
  and and_8 (and_8_out, n4_to_16_decoder_1_out[7], Write);
  and and_9 (and_9_out, Write, n4_to_16_decoder_1_out[8]);
  and and_10 (and_10_out, n4_to_16_decoder_1_out[9], Write);
  and and_11 (and_11_out, n4_to_16_decoder_1_out[10], Write);
  and and_12 (and_12_out, n4_to_16_decoder_1_out[11], Write);
  and and_13 (and_13_out, n4_to_16_decoder_1_out[12], Write);
  and and_14 (and_14_out, n4_to_16_decoder_1_out[13], Write);
  and and_15 (and_15_out, n4_to_16_decoder_1_out[14], Write);
  and and_16 (and_16_out, n4_to_16_decoder_1_out[15], Write);
  // Probe on _0_currentregister
  Register _0 (.reset(in_6), .clock(clock), .WE(1'b0), .Data(WriteData), .currentRegister(_0_currentregister));
  Register register_1 (
    .reset(in_6), .clock(clock), .WE(and_2_out), .Data(WriteData),
    .currentRegister(register_1_currentregister));
  Register _2 (.reset(in_6), .clock(clock), .WE(and_3_out), .Data(WriteData), .currentRegister(_2_currentregister));
  Register register_2 (
    .reset(in_6), .clock(clock), .WE(and_4_out), .Data(WriteData),
    .currentRegister(register_2_currentregister));
  Register _4 (.reset(in_6), .clock(clock), .WE(and_5_out), .Data(WriteData), .currentRegister(_4_currentregister));
  Register register_3 (
    .reset(in_6), .clock(clock), .WE(and_6_out), .Data(WriteData),
    .currentRegister(register_3_currentregister));
  Register _6 (.reset(in_6), .clock(clock), .WE(and_7_out), .Data(WriteData), .currentRegister(_6_currentregister));
  Register register_4 (
    .reset(in_6), .clock(clock), .WE(and_8_out), .Data(WriteData),
    .currentRegister(register_4_currentregister));
  Register _8 (.reset(in_6), .clock(clock), .WE(and_9_out), .Data(WriteData), .currentRegister(_8_currentregister));
  Register register_5 (
    .reset(in_6), .clock(clock), .WE(and_10_out), .Data(WriteData),
    .currentRegister(register_5_currentregister));
  Register _10 (.reset(in_6), .clock(clock), .WE(and_11_out), .Data(WriteData), .currentRegister(_10_currentregister));
  Register register_6 (
    .reset(in_6), .clock(clock), .WE(and_12_out), .Data(WriteData),
    .currentRegister(register_6_currentregister));
  Register _12 (.reset(in_6), .clock(clock), .WE(and_13_out), .Data(WriteData), .currentRegister(_12_currentregister));
  Register register_7 (
    .reset(in_6), .clock(clock), .WE(and_14_out), .Data(WriteData),
    .currentRegister(register_7_currentregister));
  Register _14 (.reset(in_6), .clock(clock), .WE(and_15_out), .Data(WriteData), .currentRegister(_14_currentregister));
  Register register_8 (
    .reset(in_6), .clock(clock), .WE(and_16_out), .Data(WriteData),
    .currentRegister(register_8_currentregister));
  // Probe on _2_currentregister
  // Probe on register_2_currentregister
  // Probe on _4_currentregister
  // Probe on register_3_currentregister
  // Probe on _6_currentregister
  // Probe on register_4_currentregister
  // Probe on register_1_currentregister
  RSVALPicker rsvalpicker_1 (
    .R1(_0_currentregister), .R2(register_1_currentregister), .R3(_2_currentregister),
    .R4(register_2_currentregister), .R5(_4_currentregister), .R6(register_3_currentregister),
    .R7(_6_currentregister), .R8(register_4_currentregister), .R9(_8_currentregister),
    .R10(register_5_currentregister), .R11(_10_currentregister), .R12(register_6_currentregister),
    .R13(_12_currentregister), .R14(register_7_currentregister), .R15(_14_currentregister),
    .R16(register_8_currentregister), .RS(s1), .RSVAL(RS1VAL));
  RSVALPicker rsvalpicker_2 (
    .R1(_0_currentregister), .R2(register_1_currentregister), .R3(_2_currentregister),
    .R4(register_2_currentregister), .R5(_4_currentregister), .R6(register_3_currentregister),
    .R7(_6_currentregister), .R8(register_4_currentregister), .R9(_8_currentregister),
    .R10(register_5_currentregister), .R11(_10_currentregister), .R12(register_6_currentregister),
    .R13(_12_currentregister), .R14(register_7_currentregister), .R15(_14_currentregister),
    .R16(register_8_currentregister), .RS(s2), .RSVAL(RS2VAL));
endmodule

module _4_to_16_Decoder (
  input  [3:0] \input ,
  output [15:0] out
);

  wire not_1_out, not_2_out, not_3_out, not_4_out;

  not not_1 (not_1_out, \input [0]);
  not not_2 (not_2_out, \input [1]);
  not not_3 (not_3_out, \input [2]);
  not not_4 (not_4_out, \input [3]);
  and _15 (out[15], \input [3], \input [1], \input [0], \input [2]);
  and _14 (out[14], \input [3], \input [1], not_1_out, \input [2]);
  and _12 (out[12], not_2_out, not_1_out, \input [2], \input [3]);
  and _13 (out[13], not_2_out, \input [0], \input [3], \input [2]);
  and _11 (out[11], not_3_out, \input [1], \input [0], \input [3]);
  and _10 (out[10], not_3_out, not_1_out, \input [1], \input [3]);
  and _9 (out[9], \input [3], \input [0], not_2_out, not_3_out);
  and _8 (out[8], not_2_out, not_3_out, \input [3], not_1_out);
  and _7 (out[7], not_4_out, \input [1], \input [0], \input [2]);
  and _6 (out[6], not_4_out, \input [1], not_1_out, \input [2]);
  and _5 (out[5], \input [0], not_2_out, not_4_out, \input [2]);
  and _4 (out[4], not_2_out, not_1_out, not_4_out, \input [2]);
  and _3 (out[3], not_4_out, not_3_out, \input [1], \input [0]);
  and _2 (out[2], \input [1], not_1_out, not_3_out, not_4_out);
  and _1 (out[1], \input [0], not_2_out, not_3_out, not_4_out);
  and _0 (out[0], not_1_out, not_3_out, not_2_out, not_4_out);
endmodule

module _2_to_4_Decoder (
  input  [1:0] \input ,
  output [3:0] \output 
);

  wire not_1_out, not_2_out;

  not not_1 (not_1_out, \input [1]);
  not not_2 (not_2_out, \input [0]);
  and and_1 (\output [3], \input [0], \input [1]);
  and and_2 (\output [2], not_2_out, \input [1]);
  and and_3 (\output [1], \input [0], not_1_out);
  and and_4 (\output [0], not_2_out, not_1_out);
endmodule

module Register (
  input  reset,
  input  clock,
  input  WE,
  input  [15:0] Data,
  output [15:0] currentRegister
);

  D_Flip_Flop _1 (.clk(clock), .D(Data[0]), .Q(currentRegister[0]), .en(WE), .reset(reset));  // open: Qn, preset
  D_Flip_Flop _2 (.clk(clock), .D(Data[1]), .Q(currentRegister[1]), .en(WE), .reset(reset));  // open: Qn, preset
  D_Flip_Flop _3 (.clk(clock), .D(Data[2]), .Q(currentRegister[2]), .en(WE), .reset(reset));  // open: Qn, preset
  D_Flip_Flop _1_2 (.clk(clock), .D(Data[3]), .Q(currentRegister[3]), .en(WE), .reset(reset));  // open: Qn, preset
  D_Flip_Flop _2_2 (.clk(clock), .D(Data[4]), .Q(currentRegister[4]), .en(WE), .reset(reset));  // open: Qn, preset
  D_Flip_Flop _3_2 (.clk(clock), .D(Data[5]), .Q(currentRegister[5]), .en(WE), .reset(reset));  // open: Qn, preset
  D_Flip_Flop _1_3 (.clk(clock), .D(Data[6]), .Q(currentRegister[6]), .en(WE), .reset(reset));  // open: Qn, preset
  D_Flip_Flop _2_3 (.clk(clock), .D(Data[7]), .Q(currentRegister[7]), .en(WE), .reset(reset));  // open: Qn, preset
  D_Flip_Flop _3_3 (.clk(clock), .D(Data[8]), .Q(currentRegister[8]), .en(WE), .reset(reset));  // open: Qn, preset
  D_Flip_Flop _1_4 (.clk(clock), .D(Data[9]), .Q(currentRegister[9]), .en(WE), .reset(reset));  // open: Qn, preset
  D_Flip_Flop _2_4 (.clk(clock), .D(Data[10]), .Q(currentRegister[10]), .en(WE), .reset(reset));  // open: Qn, preset
  D_Flip_Flop _3_4 (.clk(clock), .D(Data[11]), .Q(currentRegister[11]), .en(WE), .reset(reset));  // open: Qn, preset
  D_Flip_Flop _1_5 (.clk(clock), .D(Data[12]), .Q(currentRegister[12]), .en(WE), .reset(reset));  // open: Qn, preset
  D_Flip_Flop _2_5 (.clk(clock), .D(Data[13]), .Q(currentRegister[13]), .en(WE), .reset(reset));  // open: Qn, preset
  D_Flip_Flop _3_5 (.clk(clock), .D(Data[14]), .Q(currentRegister[14]), .en(WE), .reset(reset));  // open: Qn, preset
  D_Flip_Flop _3_6 (.clk(clock), .D(Data[15]), .Q(currentRegister[15]), .en(WE), .reset(reset));  // open: Qn, preset
endmodule

// DMwe
module Control (
  input  [3:0] opcode,
  output \output ,
  output \input ,
  output JAL,
  output DMwe,
  output JR,
  output JP,
  output BGT,
  output BEQZ,
  output Rwe,
  output Rwd,
  output Rdst,
  output [2:0] ALUinOP,
  output ALUinB
);

  wire [11:0] n4_to_16_decoder_1_out;
  wire [15:0] n4_to_16_decoder_2_out;

  _4_to_16_Decoder u_4_to_16_decoder_1 (
    .\input (opcode),
    .out({\input , \output , JAL, JR, n4_to_16_decoder_1_out[11], DMwe, Rwd, BEQZ, BGT, n4_to_16_decoder_1_out[6:0]}));
  _4_to_16_Decoder u_4_to_16_decoder_2 (.\input (opcode), .out(n4_to_16_decoder_2_out));
  or or_1 (ALUinOP[2], n4_to_16_decoder_2_out[4], n4_to_16_decoder_2_out[5], n4_to_16_decoder_2_out[6], n4_to_16_decoder_2_out[7], n4_to_16_decoder_2_out[8]);
  or or_2 (ALUinOP[1], n4_to_16_decoder_2_out[2], n4_to_16_decoder_2_out[3], n4_to_16_decoder_2_out[6], n4_to_16_decoder_2_out[9], n4_to_16_decoder_2_out[10]);
  or or_3 (ALUinOP[0], n4_to_16_decoder_2_out[1], n4_to_16_decoder_2_out[3], n4_to_16_decoder_2_out[5]);
  or or_4 (Rdst, n4_to_16_decoder_1_out[0], n4_to_16_decoder_1_out[1], n4_to_16_decoder_1_out[3], n4_to_16_decoder_1_out[4], n4_to_16_decoder_1_out[5], n4_to_16_decoder_1_out[6], \input );
  or or_5 (JP, n4_to_16_decoder_1_out[11], JR, JAL);
  or or_6 (Rwe, n4_to_16_decoder_1_out[0], n4_to_16_decoder_1_out[1], n4_to_16_decoder_1_out[2], n4_to_16_decoder_1_out[3], n4_to_16_decoder_1_out[4], n4_to_16_decoder_1_out[5], n4_to_16_decoder_1_out[6], Rwd, JAL, \input );
  or or_7 (ALUinB, DMwe, Rwd, n4_to_16_decoder_1_out[2]);
endmodule

module Program_Counter (
  input  [15:0] Current_PC,
  input  [5:0] immed,
  input  [15:0] s,
  input  [3:0] opcode,
  input  [11:0] address,
  output [15:0] PC_1,
  output [15:0] NextPC
);

  wire [15:0] plus_immed_sum, plus_s_2_sum, plus_s_sum;

  Multiplexer #(.select(4), .width(16), .enable("false")) multiplexer_1 (
    .in0(PC_1), .in1(PC_1), .in2(PC_1), .in3(PC_1), .in4(PC_1), .in5(PC_1), .in6(PC_1), .in7(plus_immed_sum),
    .in8(plus_immed_sum), .in9(PC_1), .in10(PC_1), .in11(plus_s_2_sum), .in12(plus_s_sum),
    .in13(plus_s_2_sum), .in14(PC_1), .in15(PC_1), .out(NextPC), .sel(opcode));
  _16_bit_adder plus_s (.in_2({16{1'b0}}), .in_3(s), .Sum(plus_s_sum));  // open: Cin, sub, Cout
  _16_bit_adder plus_s_2 (
    .in_2(Current_PC), .in_3({{5{address[11]}}, address[10:0]}), .Sum(plus_s_2_sum));  // open: Cin, sub, Cout
  _16_bit_adder plus_16 (.Cin(1'b0), .in_2(Current_PC), .in_3(16'h1), .sub(1'b0), .Sum(PC_1));  // open: Cout
  _16_bit_adder plus_immed (
    .Cin(1'b0), .in_2({{11{immed[5]}}, immed[4:0]}), .in_3(Current_PC), .sub(1'b0), .Sum(plus_immed_sum));  // open: Cout
endmodule

module RSVALPicker (
  input  [15:0] R1,
  input  [15:0] R2,
  input  [15:0] R3,
  input  [15:0] R4,
  input  [3:0] RS,
  input  [15:0] R5,
  input  [15:0] R6,
  input  [15:0] R7,
  input  [15:0] R8,
  input  [15:0] R9,
  input  [15:0] R10,
  input  [15:0] R11,
  input  [15:0] R12,
  input  [15:0] R13,
  input  [15:0] R14,
  input  [15:0] R15,
  input  [15:0] R16,
  output [15:0] RSVAL
);

  wire [15:0] n4_to_16_decoder_1_out;

  _4_to_16_Decoder u_4_to_16_decoder_1 (.\input (RS), .out(n4_to_16_decoder_1_out));
  assign RSVAL = n4_to_16_decoder_1_out[0] ? R1 : 16'bz;  // Controlled_Buffer controlled_buffer_1
  assign RSVAL = n4_to_16_decoder_1_out[1] ? R2 : 16'bz;  // Controlled_Buffer controlled_buffer_2
  assign RSVAL = n4_to_16_decoder_1_out[3] ? R4 : 16'bz;  // Controlled_Buffer controlled_buffer_3
  assign RSVAL = n4_to_16_decoder_1_out[4] ? R5 : 16'bz;  // Controlled_Buffer controlled_buffer_4
  assign RSVAL = n4_to_16_decoder_1_out[5] ? R6 : 16'bz;  // Controlled_Buffer controlled_buffer_5
  assign RSVAL = n4_to_16_decoder_1_out[6] ? R7 : 16'bz;  // Controlled_Buffer controlled_buffer_6
  assign RSVAL = n4_to_16_decoder_1_out[7] ? R8 : 16'bz;  // Controlled_Buffer controlled_buffer_7
  assign RSVAL = n4_to_16_decoder_1_out[8] ? R9 : 16'bz;  // Controlled_Buffer controlled_buffer_8
  assign RSVAL = n4_to_16_decoder_1_out[9] ? R10 : 16'bz;  // Controlled_Buffer controlled_buffer_9
  assign RSVAL = n4_to_16_decoder_1_out[10] ? R11 : 16'bz;  // Controlled_Buffer controlled_buffer_10
  assign RSVAL = n4_to_16_decoder_1_out[11] ? R12 : 16'bz;  // Controlled_Buffer controlled_buffer_11
  assign RSVAL = n4_to_16_decoder_1_out[12] ? R13 : 16'bz;  // Controlled_Buffer controlled_buffer_12
  assign RSVAL = n4_to_16_decoder_1_out[13] ? R14 : 16'bz;  // Controlled_Buffer controlled_buffer_13
  assign RSVAL = n4_to_16_decoder_1_out[14] ? R15 : 16'bz;  // Controlled_Buffer controlled_buffer_14
  assign RSVAL = n4_to_16_decoder_1_out[15] ? R16 : 16'bz;  // Controlled_Buffer controlled_buffer_15
  assign RSVAL = n4_to_16_decoder_1_out[2] ? R3 : 16'bz;  // Controlled_Buffer controlled_buffer_16
endmodule

module _2x1MUX_for_RDST (
  input  [3:0] a,
  input  [3:0] b,
  input  s,
  output [3:0] \output 
);

  wire not_1_out;
  wire [3:0] controlled_buffer_1_out, controlled_buffer_2_out;

  assign controlled_buffer_1_out = not_1_out ? a : 4'bz;  // Controlled_Buffer controlled_buffer_1
  assign controlled_buffer_2_out = s ? b : 4'bz;  // Controlled_Buffer controlled_buffer_2
  not not_1 (not_1_out, s);
  assign \output  = controlled_buffer_1_out | controlled_buffer_2_out;  // OR_Gate or_1, 4 bits wide
endmodule

module SX (
  input  [5:0] \input ,
  output [15:0] \output 
);


  assign \output  = {{11{\input [5]}}, \input [4:0]};
endmodule
